# Fritzing sketch Schematic (saved by Fritzing 1.0.4)
breadboards: 1

parts:
  C1 = Electrolytic Capacitor [capacitance=1µF voltage=35V package="100 mil [THT, electrolytic]"]
  A1 = ESP32-S3 zero
  U1 = WS2812 RGB LED strip [mn=60]
  Part1 = Logic Level Converter
  R1 = Resistor [tolerance=±5% power=0.25W resistance=330 package=THT]

nets:
  GND: C1.-, A1.Pin_2, U1.GND, Part1.GND
  5V: C1.+, A1.Pin_1, U1.VCC, Part1.HV
  N1: A1.Pin_3, Part1.LV
  N2: A1.Pin_4, Part1.RX_LV
  N3: U1.DIN, R1.Pin_1
  N4: Part1.TX_HV, R1.Pin_0

notes:
  ESP32-S3-zero board with level-shift (3.3V to 5V) on LED dataline.
  Additional capacity to support 5V rail to LEDs.
  WS2812b LED strip
  60 LEDs

custom parts:
  ESP32-S3 zero: ESP32-S3 Mini Development Board, Based on ESP32-S3FH4R2 Dual-Core Processor, 240MHz Running Frequency, 2.4GHz Wi-Fi & Bluetooth 5.
  WS2812 RGB LED strip: WS2812 strip
